// Logisim project addrdec.circ as structural Verilog: 1 circuit, main circuit main
module main (
  input  CLK,
  input  A15,
  input  A14,
  input  A13,
  input  A12,
  input  A11,
  input  A10,
  input  A9,
  input  A8,
  output RAM0,
  output RAM1,
  output VIA,
  output IRQ,
  output ACIA,
  output LCD,
  output DEV4,
  output DEV5,
  output DEV6,
  output DEV7,
  output ROM
);

  wire and_1_out, decoder_1_out0, decoder_1_out1, decoder_1_out2, decoder_1_out3, decoder_1_out4,
       decoder_1_out5, decoder_1_out6, decoder_1_out7, nand_1_out, nand_2_out, nand_3_out, nor_1_out,
       not_4_out, or_4_out;

  nand nand_1 (nand_1_out, A15, A14);
  nor nor_1 (nor_1_out, A13, A12, A11);
  nand nand_2 (nand_2_out, CLK, CLK);
  nand nand_3 (nand_3_out, CLK, A15);
  and and_1 (and_1_out, ~nand_1_out, nor_1_out);  // AND_Gate
  or or_1 (RAM1, nand_3_out, A14);
  Decoder #(.select(3)) decoder_1 (
    .out0(decoder_1_out0), .out1(decoder_1_out1), .out2(decoder_1_out2), .out3(decoder_1_out3),
    .out4(decoder_1_out4), .out5(decoder_1_out5), .out6(decoder_1_out6), .out7(decoder_1_out7),
    .sel({A10, A9, A8}), .en(and_1_out));
  or or_2 (ROM, nand_1_out, nor_1_out);
  or or_3 (RAM0, A15, nand_2_out);
  not not_1 (VIA, decoder_1_out0);
  not not_2 (IRQ, decoder_1_out1);
  not not_3 (ACIA, decoder_1_out2);
  not not_4 (not_4_out, decoder_1_out3);
  not not_5 (DEV4, decoder_1_out4);
  not not_6 (DEV5, decoder_1_out5);
  not not_7 (DEV6, decoder_1_out6);
  not not_8 (DEV7, decoder_1_out7);
  or or_4 (or_4_out, nand_2_out, not_4_out);
  nand nand_4 (LCD, or_4_out, or_4_out);
endmodule
