// Logisim project irq_rw.circ as structural Verilog: 1 circuit, main circuit main
module main (
  input  CS,
  input  RW,
  output W,
  output R
);

  wire not_1_out;

  nor nor_1 (W, CS, RW);
  not not_1 (not_1_out, CS);
  nand nand_1 (R, not_1_out, RW);
endmodule
